# Fritzing sketch NFC_RTC (saved by Fritzing 0.9.3b)
breadboards: 1

parts:
  Part1 = Arduino Uno (Rev3)
  PN532_-_NFC = Arduino Prototyping Shield
  DS3231SN = Real Time Clock Module - DS1307 RTC Breakout Board
  R1 = Resistor [tolerance=±5% resistance=220 package=THT]
  Piezo = Piezo Speaker
  LED1 = LED - 5mm [color="Red (633nm)" package="5 mm [THT]"]
  VCC1 = 4 x AAA Battery Mount
  JP2 = USB_MICROB_PLUG [package=micro-b-ra-th]
  Fox_Front_View_(Female) = DB9 Connector [package=db9]
  X1 = USB Connectors [package=usb-a-s]
  X8 = USB Connectors [package=usb-a-h]
  X9 = USB Connectors [package=usb-a-s]

nets:
  GND: Part1.GND, PN532_-_NFC.GND, DS3231SN.GND, Piezo.pin1
  N1: Part1.A4/SDA, PN532_-_NFC.SDA, DS3231SN.SDA
  N2: Part1.A5/SCL, PN532_-_NFC.SCL, DS3231SN.SCL
  N3: Part1.D2, PN532_-_NFC.D2
  N4: Part1.D3_PWM, Piezo.pin2
  N5: Part1.D4, R1.Pin_1
  N6: Part1.D6_PWM, Fox_Front_View_(Female).9
  N7: Part1.D7, Fox_Front_View_(Female).7
  5V: Part1.5V, PN532_-_NFC.+5V, DS3231SN.5V
  N8: R1.Pin_0, LED1.anode
  N9: VCC1.-, X1.GND
  N10: VCC1.+, X1.VBUS
  N11: JP2.VCC, X8.VBUS
  GND_2: JP2.GND, X8.GND
  N12: Fox_Front_View_(Female).1, X9.VBUS
  N13: Fox_Front_View_(Female).8, X9.GND

notes:
  IRQ
  USB power bank
  AAA or AA Size,
  5V, <TBD> mAh
  With USB: 90 mA (NFC:100 mA) <= UNO
  Direct: 80 mA (NFC: 90 mA)
  Tx
  Rx
  Micro USB cable
  PWM (ON = OFF = 1s)
  When Starting to Tx, Signal goes low -> Boot up NFC
  When hunt finish, this signal goes high -> Turn off NFC
  There is a 0.2xx pulse here when being to Tx and before shutdown but well after and before Fox active.
